// Logisim project control-logic.circ as structural Verilog: 1 circuit, main circuit control_logic
module control_logic (
  input  [31:0] Instruction,
  input  BrEq,
  input  BrLt,
  output PCSel,
  output RegWEn,
  output [2:0] ImmSel,
  output BrUn,
  output ASel,
  output BSel,
  output [3:0] ALUSel,
  output MemWEn,
  output [1:0] WBSel
);

  wire and_1_out, and_2_out, and_3_out, and_4_out, and_5_out, and_6_out, comparator_1_eq, comparator_2_eq,
       comparator_3_eq, comparator_4_eq, comparator_5_eq, comparator_6_eq, comparator_7_eq, comparator_8_eq,
       comparator_9_eq, comparator_10_eq, comparator_11_eq, comparator_12_eq, comparator_13_eq,
       comparator_14_eq, comparator_15_eq, comparator_16_eq, comparator_17_eq, comparator_18_eq,
       comparator_19_eq, comparator_20_eq, comparator_21_eq, comparator_22_eq, comparator_23_eq,
       comparator_24_eq, comparator_25_eq, comparator_27_eq, comparator_28_eq, comparator_29_eq,
       comparator_30_eq, comparator_31_eq, comparator_32_eq, comparator_33_eq, comparator_36_eq,
       comparator_37_eq, comparator_39_eq, comparator_40_eq, comparator_41_eq, comparator_42_eq,
       comparator_43_eq, comparator_44_eq, comparator_45_eq, comparator_46_eq, comparator_47_eq,
       comparator_48_eq, comparator_50_eq, comparator_51_eq, comparator_52_eq, comparator_53_eq,
       comparator_55_eq, comparator_56_eq, CSRSel, CSRWen, ImmSel_SB, ImmSel_U, ImmSel_UJ, isMul, isMulh,
       isSra, isSub, not_1_out, not_2_out, not_3_out, or_3_out, or_4_out, or_5_out, or_6_out, or_10_out,
       or_11_out, WBSel_ALUout, WBSel_Imm, WBSel_Mem, WBSel_PC4;
  wire [1:0] multiplexer_11_out, multiplexer_13_out;
  wire [2:0] multiplexer_1_out, multiplexer_4_out, multiplexer_6_out, multiplexer_8_out;
  wire [3:0] multiplexer_2_out, multiplexer_3_out, multiplexer_5_out, multiplexer_7_out, RIsel;
  wire [15:0] rom_1_data;

  Comparator #(.width(7)) comparator_1 (.a(Instruction[6:0]), .b(7'b1100011), .eq(comparator_1_eq));  // open: gt, lt
  Comparator #(.width(3)) comparator_2 (.a(Instruction[14:12]), .b(3'b000), .eq(comparator_2_eq));  // open: gt, lt
  Comparator #(.width(3)) comparator_3 (.a(Instruction[14:12]), .b(3'b001), .eq(comparator_3_eq));  // open: gt, lt
  Comparator #(.width(3)) comparator_4 (.a(Instruction[14:12]), .b(3'b100), .eq(comparator_4_eq));  // open: gt, lt
  Comparator #(.width(3)) comparator_5 (.a(Instruction[14:12]), .b(3'b110), .eq(comparator_5_eq));  // open: gt, lt
  Comparator #(.width(3)) comparator_6 (.a(Instruction[14:12]), .b(3'b101), .eq(comparator_6_eq));  // open: gt, lt
  Comparator #(.width(3)) comparator_7 (.a(Instruction[14:12]), .b(3'b111), .eq(comparator_7_eq));  // open: gt, lt
  Multiplexer #(.width(3)) multiplexer_1 (.in0(3'b000), .in1(3'b001), .out(multiplexer_1_out), .sel(MemWEn));
  Multiplexer #(.select(3), .width(4)) multiplexer_2 (
    .in0(4'b0000), .in1(4'b0001), .in2(4'b0010), .in4(4'b0100), .in5(4'b0101), .in6(4'b0110), .in7(4'b0111),
    .out(multiplexer_2_out), .sel(Instruction[14:12]));  // open: in3
  ROM #(.addrWidth(6), .dataWidth(16)) rom_1 (.data(rom_1_data));  // open: addr
  not not_1 (not_1_out, BrEq);
  not not_2 (not_2_out, BrLt);
  not not_3 (not_3_out, comparator_1_eq);
  Comparator #(.width(7)) comparator_8 (.a(Instruction[6:0]), .b(7'b1101111), .eq(comparator_8_eq));  // open: gt, lt
  Comparator #(.width(7)) comparator_9 (.a(Instruction[6:0]), .b(7'b0110111), .eq(comparator_9_eq));  // open: gt, lt
  Comparator #(.width(7)) comparator_10 (.a(Instruction[6:0]), .b(7'b0010111), .eq(comparator_10_eq));  // open: gt, lt
  Comparator #(.width(7)) comparator_11 (.a(Instruction[6:0]), .b(7'b1100111), .eq(comparator_11_eq));  // open: gt, lt
  Comparator #(.width(7)) comparator_12 (.a(Instruction[6:0]), .b(7'b0110011), .eq(comparator_12_eq));  // open: gt, lt
  Comparator #(.width(7)) comparator_13 (.a(Instruction[6:0]), .b(7'b0010011), .eq(comparator_13_eq));  // open: gt, lt
  Comparator #(.width(7)) comparator_14 (.a(Instruction[6:0]), .b(7'b0000011), .eq(comparator_14_eq));  // open: gt, lt
  Multiplexer #(.width(4)) multiplexer_3 (.in0(multiplexer_2_out), .in1(4'b1000), .out(multiplexer_3_out), .sel(isMul));
  Comparator #(.width(7)) comparator_15 (
    .a(Instruction[31:25]), .b(7'b0000001), .eq(comparator_15_eq));  // open: gt, lt
  Comparator #(.width(3)) comparator_16 (.a(Instruction[14:12]), .b(3'b000), .eq(comparator_16_eq));  // open: gt, lt
  Comparator #(.width(7)) comparator_17 (.a(Instruction[6:0]), .b(7'b0110011), .eq(comparator_17_eq));  // open: gt, lt
  Comparator #(.width(7)) comparator_18 (
    .a(Instruction[31:25]), .b(7'b0100000), .eq(comparator_18_eq));  // open: gt, lt
  Comparator #(.width(3)) comparator_19 (.a(Instruction[14:12]), .b(3'b000), .eq(comparator_19_eq));  // open: gt, lt
  Comparator #(.width(7)) comparator_20 (.a(Instruction[6:0]), .b(7'b0110011), .eq(comparator_20_eq));  // open: gt, lt
  Comparator #(.width(7)) comparator_21 (
    .a(Instruction[31:25]), .b(7'b0000001), .eq(comparator_21_eq));  // open: gt, lt
  Comparator #(.width(3)) comparator_22 (.a(Instruction[14:12]), .b(3'b001), .eq(comparator_22_eq));  // open: gt, lt
  Comparator #(.width(7)) comparator_23 (.a(Instruction[6:0]), .b(7'b0110011), .eq(comparator_23_eq));  // open: gt, lt
  Comparator #(.width(7)) comparator_24 (
    .a(Instruction[31:25]), .b(7'b0100000), .eq(comparator_24_eq));  // open: gt, lt
  Comparator #(.width(3)) comparator_25 (.a(Instruction[14:12]), .b(3'b101), .eq(comparator_25_eq));  // open: gt, lt
  Comparator #(.width(7)) comparator_26 (.a(Instruction[6:0]), .b(7'b0110111), .eq(WBSel_Imm));  // open: gt, lt
  Comparator #(.width(7)) comparator_27 (.a(Instruction[6:0]), .b(7'b0010111), .eq(comparator_27_eq));  // open: gt, lt
  Comparator #(.width(7)) comparator_28 (.a(Instruction[6:0]), .b(7'b0110011), .eq(comparator_28_eq));  // open: gt, lt
  Comparator #(.width(7)) comparator_29 (.a(Instruction[6:0]), .b(7'b0010011), .eq(comparator_29_eq));  // open: gt, lt
  Comparator #(.width(7)) comparator_30 (.a(Instruction[6:0]), .b(7'b1100111), .eq(comparator_30_eq));  // open: gt, lt
  Comparator #(.width(7)) comparator_31 (.a(Instruction[6:0]), .b(7'b1101111), .eq(comparator_31_eq));  // open: gt, lt
  and and_1 (and_1_out, comparator_1_eq, comparator_2_eq, BrEq);
  and and_2 (and_2_out, comparator_1_eq, comparator_3_eq, not_1_out);
  and and_3 (and_3_out, comparator_1_eq, comparator_4_eq, BrLt);
  and and_4 (and_4_out, comparator_1_eq, comparator_5_eq, BrLt);
  and and_5 (and_5_out, comparator_1_eq, comparator_6_eq, not_2_out);
  and and_6 (and_6_out, comparator_1_eq, comparator_7_eq, not_3_out);
  Comparator #(.width(7)) comparator_32 (.a(Instruction[6:0]), .b(7'b1100111), .eq(comparator_32_eq));  // open: gt, lt
  Comparator #(.width(7)) comparator_33 (.a(Instruction[6:0]), .b(7'b1101111), .eq(comparator_33_eq));  // open: gt, lt
  Multiplexer #(.width(3)) multiplexer_4 (
    .in0(multiplexer_1_out), .in1(3'b010), .out(multiplexer_4_out), .sel(ImmSel_SB));
  Comparator #(.width(7)) comparator_34 (.a(Instruction[6:0]), .b(7'b1110011), .eq(CSRWen));  // open: gt, lt
  Multiplexer #(.width(4)) multiplexer_5 (.in0(multiplexer_3_out), .in1(4'b1100), .out(multiplexer_5_out), .sel(isSub));
  and and_7 (isMul, comparator_15_eq, comparator_16_eq, comparator_17_eq);
  and and_8 (isSub, comparator_18_eq, comparator_19_eq, comparator_20_eq);
  and and_9 (isMulh, comparator_21_eq, comparator_22_eq, comparator_23_eq);
  and and_10 (isSra, comparator_24_eq, comparator_25_eq);
  or or_1 (WBSel_ALUout, comparator_27_eq, comparator_28_eq, comparator_29_eq);
  or or_2 (WBSel_PC4, comparator_30_eq, comparator_31_eq);
  Multiplexer #(.width(3)) multiplexer_6 (
    .in0(multiplexer_4_out), .in1(3'b011), .out(multiplexer_6_out), .sel(ImmSel_U));
  Multiplexer #(.width(4)) multiplexer_7 (
    .in0(multiplexer_5_out), .in1(4'b1001), .out(multiplexer_7_out), .sel(isMulh));
  or or_3 (or_3_out, and_1_out, and_2_out, and_3_out, and_4_out, and_5_out, and_6_out);
  or or_4 (or_4_out, comparator_32_eq, comparator_33_eq);
  Comparator #(.width(7)) comparator_35 (.a(Instruction[6:0]), .b(7'b0100011), .eq(MemWEn));  // open: gt, lt
  Multiplexer #(.width(3)) multiplexer_8 (
    .in0(multiplexer_6_out), .in1(3'b100), .out(multiplexer_8_out), .sel(ImmSel_UJ));
  or or_5 (or_5_out, comparator_8_eq, comparator_9_eq, comparator_10_eq);
  or or_6 (or_6_out, comparator_12_eq, comparator_13_eq, comparator_14_eq);
  Multiplexer #(.width(4)) multiplexer_9 (.in0(multiplexer_7_out), .in1(4'b1101), .out(RIsel), .sel(isSra));
  Comparator #(.width(7)) comparator_36 (.a(Instruction[6:0]), .b(7'b0010111), .eq(comparator_36_eq));  // open: gt, lt
  Comparator #(.width(7)) comparator_37 (.a(Instruction[6:0]), .b(7'b1101111), .eq(comparator_37_eq));  // open: gt, lt
  or or_7 (PCSel, or_3_out, or_4_out);
  or or_8 (RegWEn, or_5_out, comparator_11_eq, or_6_out);
  Multiplexer #(.width(3)) multiplexer_10 (.in0(multiplexer_8_out), .in1(3'b101), .out(ImmSel), .sel(CSRSel));
  Comparator #(.width(7)) comparator_38 (.a(Instruction[6:0]), .b(7'b0000011), .eq(WBSel_Mem));  // open: gt, lt
  Multiplexer #(.width(2)) multiplexer_11 (.in0(2'b00), .in1(2'b01), .out(multiplexer_11_out), .sel(WBSel_ALUout));
  or or_9 (ASel, comparator_1_eq, comparator_36_eq, comparator_37_eq);
  Comparator #(.width(7)) comparator_39 (.a(Instruction[6:0]), .b(7'b0110011), .eq(comparator_39_eq));  // open: gt, lt
  Comparator #(.width(7)) comparator_40 (.a(Instruction[6:0]), .b(7'b0010011), .eq(comparator_40_eq));  // open: gt, lt
  Multiplexer #(.width(4)) multiplexer_12 (.in0(4'b0000), .in1(RIsel), .out(ALUSel), .sel(or_10_out));
  or or_10 (or_10_out, comparator_39_eq, comparator_40_eq);
  Multiplexer #(.width(2)) multiplexer_13 (
    .in0(multiplexer_11_out), .in1(2'b10), .out(multiplexer_13_out), .sel(WBSel_PC4));
  Multiplexer #(.width(2)) multiplexer_14 (.in0(multiplexer_13_out), .in1(2'b11), .out(WBSel), .sel(WBSel_Mem));
  Comparator #(.width(7)) comparator_41 (.a(Instruction[6:0]), .b(7'b0010011), .eq(comparator_41_eq));  // open: gt, lt
  Comparator #(.width(7)) comparator_42 (.a(Instruction[6:0]), .b(7'b0000011), .eq(comparator_42_eq));  // open: gt, lt
  Comparator #(.width(7)) comparator_43 (.a(Instruction[6:0]), .b(7'b1100011), .eq(comparator_43_eq));  // open: gt, lt
  Comparator #(.width(7)) comparator_44 (.a(Instruction[6:0]), .b(7'b1100111), .eq(comparator_44_eq));  // open: gt, lt
  Comparator #(.width(7)) comparator_45 (.a(Instruction[6:0]), .b(7'b0010111), .eq(comparator_45_eq));  // open: gt, lt
  Comparator #(.width(7)) comparator_46 (.a(Instruction[6:0]), .b(7'b0110111), .eq(comparator_46_eq));  // open: gt, lt
  Comparator #(.width(7)) comparator_47 (.a(Instruction[6:0]), .b(7'b1101111), .eq(comparator_47_eq));  // open: gt, lt
  Comparator #(.width(7)) comparator_48 (.a(Instruction[6:0]), .b(7'b0100011), .eq(comparator_48_eq));  // open: gt, lt
  Comparator #(.width(7)) comparator_49 (.a(Instruction[6:0]), .b(7'b1100011), .eq(ImmSel_SB));  // open: gt, lt
  Comparator #(.width(3)) comparator_50 (.a(Instruction[14:12]), .b(3'b110), .eq(comparator_50_eq));  // open: gt, lt
  Comparator #(.width(3)) comparator_51 (.a(Instruction[14:12]), .b(3'b111), .eq(comparator_51_eq));  // open: gt, lt
  or or_11 (or_11_out, comparator_50_eq, comparator_51_eq);
  and and_11 (BrUn, ImmSel_SB, or_11_out);
  or or_12 (BSel, comparator_41_eq, comparator_42_eq, comparator_43_eq, comparator_44_eq, comparator_45_eq, comparator_46_eq, comparator_47_eq, comparator_48_eq);
  Comparator #(.width(7)) comparator_52 (.a(Instruction[6:0]), .b(7'b0010111), .eq(comparator_52_eq));  // open: gt, lt
  Comparator #(.width(7)) comparator_53 (.a(Instruction[6:0]), .b(7'b0110111), .eq(comparator_53_eq));  // open: gt, lt
  Comparator #(.width(7)) comparator_54 (.a(Instruction[6:0]), .b(7'b1101111), .eq(ImmSel_UJ));  // open: gt, lt
  Comparator #(.width(7)) comparator_55 (.a(Instruction[6:0]), .b(7'b1110011), .eq(comparator_55_eq));  // open: gt, lt
  Comparator #(.width(3)) comparator_56 (.a(Instruction[14:12]), .b(3'b101), .eq(comparator_56_eq));  // open: gt, lt
  or or_13 (ImmSel_U, comparator_52_eq, comparator_53_eq);
  and and_12 (CSRSel, comparator_55_eq, comparator_56_eq);

  // Other names for the same wires on the sheet: ImmSel_S = MemWEn; ImmSel_CSRRWI = CSRSel;
  //   opcode[6:0] = Instruction[6:0]; rd[4:0] = Instruction[11:7]; func3[2:0] = Instruction[14:12];
  //   rs1[4:0] = Instruction[19:15]; rs2[4:0] = Instruction[24:20]; func7[6:0] = Instruction[31:25]

  // Notes on the sheet:
  //   Decode
  //   INPUTS to your circuit
  //   ALUSel
  //   jal
  //   Connect ROM Input here ->
  //   PCsel, Asel, Bsel
  //   WBSel
  //   lui
  //   auipc
  //   R
  //   I
  //   jalr
  //   PC选择逻辑，选PC+4还是立即数
  //   immSel, BrUn,MemRW
  //   jal
  //   lui
  //   auipc
  //   jalr
  //   R
  //   I
  //   load
  //   ROM FOR CONTROL LOGIC
  //   beq
  //   bnq
  //   blt
  //   bltu
  //   bge
  //   bgeu
  //   Reg写回逻辑
  //   csrrw
  //   jalr
  //   jal
  //   DON'T CHANGE THE LOCATIONS OF THE INPUTS AND OUTPUTS!
  //   This is only if you choose to do the ROM option
  //   CONNECT
  //   WIRE
  //   TO
  //   USE
  //   ROM
  //   OUTPUT from your circuit
  //   R-instr
  //   I-instr
  //   Asel:计算数a，选rs1还是PC
  //   lui
  //   写回逻辑：立即数、ALU、PC+4
  //   除了R和I型计算指令，其余都默认加法
  //   Reminder: If using ROM, use combinational logic for PCSel
  //   立即数选取逻辑：0 -- 5
  //   Bsel: 计算数b，选rs2还是imm
endmodule
