// Logisim project cpu.circ as structural Verilog: 1 circuit, main circuit cpu
module cpu (
  input  clk,
  input  [31:0] Instruction,
  input  [31:0] MemReadData,
  output [31:0] MemAddress,
  output [31:0] ProgramCounter,
  output [31:0] ra,
  output [31:0] sp,
  output [31:0] t0,
  output [31:0] t1,
  output [31:0] t2,
  output [31:0] s0,
  output [31:0] s1,
  output [31:0] a0,
  output [3:0] MemWriteMask,
  output [31:0] MemWriteData
);

  wire Asel, BrEq, BrLt, BrUn, Bsel, MemWEn, PCSel, RegWEn;
  wire [1:0] WBSel;
  wire [2:0] func3, ImmSel;
  wire [3:0] ALUSel;
  wire [6:0] func7;
  wire [24:0] Instruction_t;
  wire [31:0] adder_1_out, DataRead, imm_data, multiplexer_1_out, multiplexer_3_out, multiplexer_4_out,
       multiplexer_5_out, PCp4, ProgramCounter_t, r1, r2, WBData;

  Adder #(.width(32)) adder_1 (.a(ProgramCounter), .b(32'h4), .out(adder_1_out));  // open: cin, cout
  Multiplexer #(.width(32)) multiplexer_1 (.in0(adder_1_out), .in1(MemAddress), .out(multiplexer_1_out), .sel(PCSel));
  Register #(.width(32)) PC (.D(multiplexer_1_out), .clk(clk), .Q(ProgramCounter));  // open: en, clr
  Multiplexer #(.select(2), .width(32)) multiplexer_2 (
    .in0(imm_data), .in1(MemAddress), .in2(PCp4), .in3(DataRead), .out(WBData), .sel(WBSel));
  Adder #(.width(32)) adder_2 (.a(ProgramCounter), .b(32'h4), .out(PCp4));  // open: cin, cout
  control_logic control_logic_1 (
    .Instruction({func7, Instruction_t[24:15], func3, Instruction_t[11:0]}), .BrEq(BrEq), .BrLt(BrLt),
    .PCSel(PCSel), .RegWEn(RegWEn), .ImmSel(ImmSel), .BrUn(BrUn), .ASel(Asel), .BSel(Bsel), .ALUSel(ALUSel),
    .MemWEn(MemWEn), .WBSel(WBSel));
  regfile regfile_1 (
    .ReadIndex1(Instruction_t[19:15]), .ReadIndex2(Instruction_t[24:20]), .WriteIndex(Instruction_t[11:7]),
    .WriteData(WBData), .RegWEn(RegWEn), .clk(clk), .ra(ra), .sp(sp), .t0(t0), .t1(t1), .t2(t2), .s0(s0),
    .s1(s1), .a0(a0), .ReadData1(r1), .ReadData2(r2));
  imm_gen imm_gen_1 (
    .Instruction({func7, Instruction_t[24:15], func3, Instruction_t[11:0]}), .ImmSel(ImmSel),
    .Immediate(imm_data));
  Multiplexer #(.width(32)) multiplexer_3 (.in0(Instruction), .in1(32'h13), .out(multiplexer_3_out), .sel(PCSel));
  Register #(.width(32)) register_1 (
    .D(multiplexer_3_out), .clk(clk), .Q({func7, Instruction_t[24:15], func3, Instruction_t[11:0]}));  // open: en, clr
  Multiplexer #(.width(32)) multiplexer_4 (.in0(r1), .in1(ProgramCounter_t), .out(multiplexer_4_out), .sel(Asel));
  Multiplexer #(.width(32)) multiplexer_5 (.in0(r2), .in1(imm_data), .out(multiplexer_5_out), .sel(Bsel));
  alu alu_1 (.A(multiplexer_4_out), .B(multiplexer_5_out), .ALUSel(ALUSel), .ALUResult(MemAddress));
  branch_comp branch_comp_1 (.BrData1(r1), .BrData2(r2), .BrUn(BrUn), .BrEq(BrEq), .BrLt(BrLt));
  Register #(.width(32)) register_2 (.D(ProgramCounter), .clk(clk), .Q(ProgramCounter_t));  // open: en, clr
  partial_store partial_store_1 (
    .Instruction({func7, Instruction_t[24:15], func3, Instruction_t[11:0]}), .MemAddress(MemAddress),
    .DataFromReg(r2), .MemWEn(MemWEn), .MemWriteMask(MemWriteMask), .DataToMem(MemWriteData));
  partial_load partial_load_1 (
    .Instruction({func7, Instruction_t[24:15], func3, Instruction_t[11:0]}), .MemAddress(MemAddress),
    .DataFromMem(MemReadData), .DataToReg(DataRead));

  // Other names for the same wires on the sheet: ALUresult[31:0] = MemAddress; opcode[6:0] = Instruction_t[6:0];
  //   rd[4:0] = Instruction_t[11:7]; Instruction_t (some bits) = {func7, func3}; rs1[4:0] = Instruction_t[19:15];
  //   rs2[4:0] = Instruction_t[24:20]; NextInstruction[31:0] = Instruction; NextProgramCounter[31:0] = ProgramCounter

  // Notes on the sheet:
  //   Decode
  //   Writebackdata
  //   To IMEM
  //   IMEM (do **NOT** move this)
  //   From IMEM
  //   intermediate reg
  //   Inputs/Outputs for testing. Do **NOT** move these.
  //   It is OK to move the PC, RegFile, ALU, MEM, Branch Comp, Imm Gen, Partial Load, Partial Store and Control Logic to wherever is most convenient for you when constructing your CPU, and to delete this text
  //   To DMEM
  //   DMEM (do **NOT** move this)
  //   From DMEM
endmodule
