// Logisim project partial-store.circ as structural Verilog: 1 circuit, main circuit partial_store
module partial_store (
  input  [31:0] Instruction,
  input  [31:0] MemAddress,
  input  [31:0] DataFromReg,
  input  MemWEn,
  output [3:0] MemWriteMask,
  output [31:0] DataToMem
);

  wire comparator_1_eq, comparator_2_eq, comparator_3_eq, comparator_4_eq, comparator_5_eq, comparator_6_eq,
       comparator_7_eq;
  wire [15:0] undriven_6;
  wire [23:0] undriven_4;
  wire [31:0] multiplexer_1_out, multiplexer_2_out, undriven_2, undriven_3;
  wire [31:8] undriven;
  wire [31:16] undriven_5;

  Multiplexer #(.select(2), .width(32)) multiplexer_1 (
    .in0({undriven, DataFromReg[7:0]}), .in1({undriven_2[31:16], DataFromReg[7:0], undriven_2[7:0]}),
    .in2({undriven_3[31:24], DataFromReg[7:0], undriven_3[15:0]}), .in3({DataFromReg[7:0], undriven_4}),
    .out(multiplexer_1_out), .sel(MemAddress[1:0]));
  Multiplexer #(.select(2), .width(32)) multiplexer_2 (
    .in0({undriven_5, DataFromReg[15:0]}), .in2({DataFromReg[15:0], undriven_6}), .out(multiplexer_2_out),
    .sel(MemAddress[1:0]));  // open: in1, in3
  Multiplexer #(.select(3), .width(32)) multiplexer_3 (
    .in0(multiplexer_1_out), .in1(multiplexer_2_out), .in2(DataFromReg), .out(DataToMem),
    .sel(Instruction[14:12]));  // open: in3, in4, in5, in6, in7
  Comparator #(.width(5)) comparator_1 (
    .a({Instruction[14:12], MemAddress[1:0]}), .b({5{1'b0}}), .eq(comparator_1_eq));  // open: gt, lt
  Comparator #(.width(5)) comparator_2 (
    .a({Instruction[14:12], MemAddress[1:0]}), .b(5'b00001), .eq(comparator_2_eq));  // open: gt, lt
  Comparator #(.width(5)) comparator_3 (
    .a({Instruction[14:12], MemAddress[1:0]}), .b(5'b00010), .eq(comparator_3_eq));  // open: gt, lt
  Comparator #(.width(5)) comparator_4 (
    .a({Instruction[14:12], MemAddress[1:0]}), .b(5'b00011), .eq(comparator_4_eq));  // open: gt, lt
  Comparator #(.width(5)) comparator_5 (
    .a({Instruction[14:12], MemAddress[1:0]}), .b(5'b00100), .eq(comparator_5_eq));  // open: gt, lt
  Comparator #(.width(5)) comparator_6 (
    .a({Instruction[14:12], MemAddress[1:0]}), .b(5'b00110), .eq(comparator_6_eq));  // open: gt, lt
  Comparator #(.width(5)) comparator_7 (
    .a({Instruction[14:12], MemAddress[1:0]}), .b(5'b01000), .eq(comparator_7_eq));  // open: gt, lt
  Priority_Encoder #(.select_enc(4)) priority_encoder_1 (
    .in1(comparator_1_eq), .in2(comparator_2_eq), .in3(comparator_5_eq), .in4(comparator_3_eq),
    .in8(comparator_4_eq), .in12(comparator_6_eq), .in15(comparator_7_eq), .out(MemWriteMask), .en_in(MemWEn));  // open: in0, in5, in6, in7, in9, in10, in11, in13, in14, gs, en_out

  // Other names for the same wires on the sheet: f3b2[4:0] = {Instruction[14:12], MemAddress[1:0]}

  // Notes on the sheet:
  //   INPUTS to your circuit
  //   DON'T CHANGE THE LOCATIONS OF THE INPUTS AND OUTPUTS!
  //   OUTPUT from your circuit
endmodule
